# Fritzing sketch Fritzing_controleur_MIDI (saved by Fritzing 0.9.3b)
perfboards: 1

parts:
  R1 = Slide Potentiometer [maximum_resistance=100kΩ]
  R2 = Slide Potentiometer [maximum_resistance=100kΩ]
  R3 = Slide Potentiometer [maximum_resistance=100kΩ]
  R4 = Slide Potentiometer [maximum_resistance=100kΩ]
  RE1 = Rotary Encoder [package=THT]  # not connected
  RE2 = Rotary Encoder [package=THT]  # not connected
  RE3 = Rotary Encoder [package=THT]  # not connected
  RE4 = Rotary Encoder [package=THT]  # not connected
  J1 = Basic Force Sensing Resistor (FSR) [package=THT]  # not connected
  J2 = Basic Force Sensing Resistor (FSR) [package=THT]  # not connected
  J3 = Basic Force Sensing Resistor (FSR) [package=THT]  # not connected
  J4 = Basic Force Sensing Resistor (FSR) [package=THT]  # not connected
  Composant2 = Arduino Mega 2560 (Rev3)

nets:
  N1: R1.leg1, R2.leg1, R3.leg1, R4.leg1, Composant2.GND
  N2: R1.wiper, R2.wiper, R3.wiper, R4.wiper
